# Fritzing sketch 312-313-BLINKANJE_DVIJE_LED_DIODE (saved by Fritzing 0.9.0b)
breadboards: 1

parts:
  Part1 = Arduino Uno (Rev3)
  R1 = Resistor [tolerance=±5% resistance=330 package=THT]
  LED1 = LED - 5mm [color="Red (635nm)" package="5 mm [THT]"]
  R2 = Resistor [tolerance=±5% resistance=330 package=THT]
  LED2 = LED - 5mm [color="Red (635nm)" package="5 mm [THT]"]

nets:
  N1: Part1.D2, R1.Pin_0
  N2: Part1.D3_PWM, R2.Pin_0
  N3: Part1.GND, LED1.cathode, LED2.cathode
  N4: R1.Pin_1, LED1.anode
  N5: R2.Pin_1, LED2.anode
