# Fritzing sketch 316-SEMAFOR_ZA_AUTOMOBILE (saved by Fritzing 1.0.4)
breadboards: 1

parts:
  DC1 = Dasduino CORE [part_number=333037]
  R1 = Resistor [tolerance=±5% power=0.25W resistance=330 package=THT]
  LED1 = LED - 5mm [color="Red (633nm)" current=0.030A package="5 mm [THT]"]
  LED2 = LED - 5mm [color="Yellow (595nm)" current=0.030A package="5 mm [THT]"]
  R2 = Resistor [tolerance=±5% power=0.25W resistance=330 package=THT]
  LED3 = LED - 5mm [color="Green (555nm)" current=0.030A package="5 mm [THT]"]
  R3 = Resistor [tolerance=±5% power=0.25W resistance=330 package=THT]

nets:
  N1: DC1.GND, LED1.cathode, LED2.cathode, LED3.cathode
  N2: DC1.D4, R3.Pin_0
  N3: DC1.D3, R2.Pin_0
  N4: DC1.D2, R1.Pin_0
  N5: R1.Pin_1, LED1.anode
  N6: LED2.anode, R2.Pin_1
  N7: LED3.anode, R3.Pin_1

custom parts:
  Dasduino CORE: Soldered Dasduino CORE (V1.1.1): pločica kompatibilna s Arduinom, ATmega328P na 16 MHz, 5 V, USB-C s CH340C, punjač Li-ion baterije, priključak easyC, RGB LED na D8, tipka USER na D7, LED na D13. Obris 63 x 25,86 mm; izvodi 2 x 15 u rasteru 2,54 mm, razmak redova 22,86 mm (0,9 in). Mjere prema Solderedovom KiCad projektu (TAPR OHL); raspored izvoda Soldered, CC BY-SA 4.0.
