# Fritzing sketch 331-332-333-7SEGMENT (saved by Fritzing 1.0.4)
breadboards: 1

parts:
  DC1 = Dasduino CORE [part_number=333037]
  7_Segment1 = 7 Segment Display
  R1 = Resistor [tolerance=±5% power=0.25W resistance=220 package=THT]
  R2 = Resistor [tolerance=±5% power=0.25W resistance=220 package=THT]
  R3 = Resistor [tolerance=±5% power=0.25W resistance=220 package=THT]
  R4 = Resistor [tolerance=±5% power=0.25W resistance=220 package=THT]
  R5 = Resistor [tolerance=±5% power=0.25W resistance=220 package=THT]
  R6 = Resistor [tolerance=±5% power=0.25W resistance=220 package=THT]
  R7 = Resistor [tolerance=±5% power=0.25W resistance=220 package=THT]

nets:
  N1: DC1.D6, R5.Pin_0
  N2: DC1.D9, R6.Pin_0
  N3: DC1.D10, R7.Pin_0
  N4: DC1.GND, 7_Segment1.common_cathode
  N5: DC1.D5, R4.Pin_0
  N6: DC1.D4, R3.Pin_1
  N7: DC1.D3, R2.Pin_1
  N8: DC1.D2, R1.Pin_1
  N9: 7_Segment1.Segment_E, R5.Pin_1
  N10: 7_Segment1.Segment_D, R4.Pin_1
  N11: 7_Segment1.Segment_C, R3.Pin_0
  N12: 7_Segment1.Segment_B, R2.Pin_0
  N13: 7_Segment1.Segment_A, R1.Pin_0
  N14: 7_Segment1.Segment_F, R6.Pin_1
  N15: 7_Segment1.Segment_G, R7.Pin_1

custom parts:
  Dasduino CORE: Soldered Dasduino CORE (V1.1.1): pločica kompatibilna s Arduinom, ATmega328P na 16 MHz, 5 V, USB-C s CH340C, punjač Li-ion baterije, priključak easyC, RGB LED na D8, tipka USER na D7, LED na D13. Obris 63 x 25,86 mm; izvodi 2 x 15 u rasteru 2,54 mm, razmak redova 22,86 mm (0,9 in). Mjere prema Solderedovom KiCad projektu (TAPR OHL); raspored izvoda Soldered, CC BY-SA 4.0.
