# Fritzing sketch 413-417-UKLJUCI-ISKLJUCI_S_DVA_TIPKALA (saved by Fritzing 1.0.4)
breadboards: 1

parts:
  DC1 = Dasduino CORE [part_number=333037]
  R1 = Resistor [tolerance=±5% power=0.25W resistance=330 package=THT]
  LED1 = smd LED [color="Red (633nm)" package="0805 [SMD]"]
  S1 = Momentary Switch [package=ksa_sealed_tac_switch]
  S2 = Momentary Switch [package=ksa_sealed_tac_switch]

nets:
  N1: DC1.GND, LED1.cathode, S1.4, S2.4
  N2: DC1.D4, S2.1
  N3: DC1.D3, S1.1
  N4: DC1.D2, R1.Pin_1
  N5: R1.Pin_0, LED1.anode

custom parts:
  Dasduino CORE: Soldered Dasduino CORE (V1.1.1): pločica kompatibilna s Arduinom, ATmega328P na 16 MHz, 5 V, USB-C s CH340C, punjač Li-ion baterije, priključak easyC, RGB LED na D8, tipka USER na D7, LED na D13. Obris 63 x 25,86 mm; izvodi 2 x 15 u rasteru 2,54 mm, razmak redova 22,86 mm (0,9 in). Mjere prema Solderedovom KiCad projektu (TAPR OHL); raspored izvoda Soldered, CC BY-SA 4.0.
