# Fritzing sketch 414-TRCECE_SVIJETLO_LIJEVO_DESNO (saved by Fritzing 0.9.0b)
breadboards: 1

parts:
  Part1 = Arduino Uno (Rev3)
  R1 = Resistor [tolerance=±5% resistance=330 package=THT]
  LED1 = LED - 5mm [color="Red (635nm)" package="5 mm [THT]"]
  R2 = Resistor [tolerance=±5% resistance=330 package=THT]
  LED2 = LED - 5mm [color="Red (635nm)" package="5 mm [THT]"]
  R3 = Resistor [tolerance=±5% resistance=330 package=THT]
  LED3 = LED - 5mm [color="Red (635nm)" package="5 mm [THT]"]
  S3 = Momentary Switch [package=ksa_sealed_tac_switch]
  S4 = Momentary Switch [package=ksa_sealed_tac_switch]

nets:
  N1: Part1.D2, R1.Pin_0
  N2: Part1.D3_PWM, R2.Pin_0
  N3: Part1.D4, R3.Pin_0
  N4: Part1.D5_PWM, S3.1
  N5: Part1.D6_PWM, S4.1
  N6: Part1.GND, LED1.cathode, LED2.cathode, LED3.cathode, S3.4, S4.4
  N7: R1.Pin_1, LED1.anode
  N8: R2.Pin_1, LED2.anode
  N9: R3.Pin_1, LED3.anode
