# Fritzing sketch 421-KLIMA (saved by Fritzing 0.9.0b)
breadboards: 1

parts:
  Part1 = Arduino Uno (Rev3)
  R1 = Resistor [tolerance=±5% resistance=330 package=THT]
  LED1 = LED - 5mm [color="Red (635nm)" package="5 mm [THT]"]
  SW1 = DIP SWITCH [package=dipswitch-02]
  S1 = Reed switch [package=THT]

nets:
  N1: Part1.GND, LED1.cathode, SW1.1, S1.pin_1
  N2: Part1.D2, R1.Pin_0
  N3: Part1.D3_PWM, SW1.4
  N4: Part1.D4, S1.pin_2
  N5: R1.Pin_1, LED1.anode
