# Fritzing sketch 51-KOCKA (saved by Fritzing 0.9.0b)
breadboards: 1

parts:
  Part1 = Arduino Uno (Rev3)
  R1 = Resistor [tolerance=±5% resistance=330 package=THT]
  R2 = Resistor [tolerance=±5% resistance=330 package=THT]
  R3 = Resistor [tolerance=±5% resistance=330 package=THT]
  S3 = Momentary Switch [package=ksa_sealed_tac_switch]
  LED4 = LED - 5mm [color="Red (635nm)" package="5 mm [THT]"]
  LED3 = LED - 5mm [color="Red (635nm)" package="5 mm [THT]"]
  LED6 = LED - 5mm [color="Red (635nm)" package="5 mm [THT]"]
  LED7 = LED - 5mm [color="Red (635nm)" package="5 mm [THT]"]
  LED5 = LED - 5mm [color="Red (635nm)" package="5 mm [THT]"]
  LED2 = LED - 5mm [color="Red (635nm)" package="5 mm [THT]"]
  LED1 = LED - 5mm [color="Red (635nm)" package="5 mm [THT]"]
  R4 = Resistor [tolerance=±5% resistance=330 package=THT]
  R5 = Resistor [tolerance=±5% resistance=330 package=THT]
  R6 = Resistor [tolerance=±5% resistance=330 package=THT]
  R7 = Resistor [tolerance=±5% resistance=330 package=THT]

nets:
  N1: Part1.D8, R1.Pin_0
  N2: Part1.D9_PWM, S3.1
  N3: Part1.D2, R6.Pin_0
  N4: Part1.D3_PWM, R5.Pin_0
  N5: Part1.D4, R4.Pin_0
  N6: Part1.D5_PWM, R7.Pin_0
  N7: Part1.D6_PWM, R3.Pin_0
  N8: Part1.D7, R2.Pin_0
  N9: Part1.GND, S3.4, LED4.cathode, LED3.cathode, LED6.cathode, LED7.cathode, LED5.cathode, LED2.cathode, LED1.cathode
  N10: R1.Pin_1, LED5.anode
  N11: R2.Pin_1, LED6.anode
  N12: R3.Pin_1, LED7.anode
  N13: LED4.anode, R7.Pin_1
  N14: LED3.anode, R4.Pin_1
  N15: LED2.anode, R5.Pin_1
  N16: LED1.anode, R6.Pin_1
