# Fritzing sketch 52-DIZALO (saved by Fritzing 0.9.0b)
breadboards: 1

parts:
  Part1 = Arduino Uno (Rev3)
  R3 = Resistor [tolerance=±5% resistance=330 package=THT]
  R5 = Resistor [tolerance=±5% resistance=330 package=THT]
  R6 = Resistor [tolerance=±5% resistance=330 package=THT]
  R7 = Resistor [tolerance=±5% resistance=330 package=THT]
  R8 = Resistor [tolerance=±5% resistance=330 package=THT]
  R9 = Resistor [tolerance=±5% resistance=330 package=THT]
  R4 = Resistor [tolerance=±5% resistance=330 package=THT]
  R2 = Resistor [tolerance=±5% resistance=330 package=THT]
  7_Segment1 = 7 Segment Display
  S1 = Reed switch [package=THT]
  S2 = Reed switch [package=THT]
  S3 = Reed switch [package=THT]

nets:
  N1: Part1.D8, R2.Pin_0
  N2: Part1.D9_PWM, R9.Pin_1
  N3: Part1.D10_PWM/SS, S1.pin_2
  N4: Part1.D11_PWM/MOSI, S2.pin_2
  N5: Part1.D12/MISO, S3.pin_2
  N6: Part1.D2, R4.Pin_1
  N7: Part1.D3_PWM, R5.Pin_1
  N8: Part1.D4, R8.Pin_1
  N9: Part1.D5_PWM, R7.Pin_0
  N10: Part1.D6_PWM, R6.Pin_0
  N11: Part1.D7, R3.Pin_0
  N12: Part1.GND, 7_Segment1.common_cathode, S1.pin_1, S2.pin_1, S3.pin_1
  N13: R3.Pin_1, 7_Segment1.Segment_F
  N14: R5.Pin_0, 7_Segment1.Segment_B
  N15: R6.Pin_1, 7_Segment1.Segment_E
  N16: R7.Pin_1, 7_Segment1.Segment_D
  N17: R8.Pin_0, 7_Segment1.Segment_C
  N18: R9.Pin_0, 7_Segment1.Segment_DP
  N19: R4.Pin_0, 7_Segment1.Segment_A
  N20: R2.Pin_1, 7_Segment1.Segment_G
