# Fritzing sketch 612-613-SINGLELEDDIM (saved by Fritzing 0.9.0b)
breadboards: 1

parts:
  Part1 = Arduino Uno (Rev3)
  R1 = Resistor [tolerance=±5% resistance=330 package=THT]
  LED1 = LED - 5mm [color="Red (635nm)" package="5 mm [THT]"]

nets:
  N1: Part1.GND, LED1.cathode
  N2: Part1.D3_PWM, R1.Pin_0
  N3: R1.Pin_1, LED1.anode
