# Fritzing sketch 621-RGB (saved by Fritzing 0.9.0b)
breadboards: 1

parts:
  Part1 = Arduino Uno (Rev3)
  R1 = Resistor [tolerance=±5% resistance=330 package=THT]
  R2 = Resistor [tolerance=±5% resistance=330 package=THT]
  R3 = Resistor [tolerance=±5% resistance=330 package=THT]
  LED6 = RGB LED - (4 legs) [package="5 mm [THT]"]

nets:
  N1: Part1.D3_PWM, R1.Pin_0
  N2: Part1.D5_PWM, R2.Pin_0
  N3: Part1.D6_PWM, R3.Pin_0
  N4: Part1.5V, LED6.common_anode
  N5: R1.Pin_1, LED6.red_cathode
  N6: R2.Pin_1, LED6.green_cathode
  N7: R3.Pin_1, LED6.blue_cathode
