# Fritzing sketch 622-ALLCOLORDIMMER (saved by Fritzing 0.9.0b)
breadboards: 1

parts:
  Part1 = Arduino Uno (Rev3)
  R1 = Resistor [tolerance=±5% resistance=330 package=THT]
  R2 = Resistor [tolerance=±5% resistance=330 package=THT]
  R3 = Resistor [tolerance=±5% resistance=330 package=THT]
  LED6 = RGB LED - (4 legs) [package="5 mm [THT]"]
  S1 = Momentary Switch [package=ksa_sealed_tac_switch]
  S2 = Momentary Switch [package=ksa_sealed_tac_switch]
  S3 = Momentary Switch [package=ksa_sealed_tac_switch]
  S4 = Momentary Switch [package=ksa_sealed_tac_switch]
  S5 = Momentary Switch [package=ksa_sealed_tac_switch]
  S6 = Momentary Switch [package=ksa_sealed_tac_switch]

nets:
  N1: Part1.D8, S1.1
  N2: Part1.D9_PWM, S2.1
  N3: Part1.D10_PWM/SS, S3.1
  N4: Part1.D11_PWM/MOSI, S4.1
  N5: Part1.D12/MISO, S5.1
  N6: Part1.D13/SCK, S6.1
  N7: Part1.D3_PWM, R1.Pin_0
  N8: Part1.D5_PWM, R2.Pin_0
  N9: Part1.D6_PWM, R3.Pin_0
  N10: Part1.5V, LED6.common_anode
  N11: Part1.GND, S1.4, S2.4, S3.4, S4.4, S5.4, S6.4
  N12: R1.Pin_1, LED6.red_cathode
  N13: R2.Pin_1, LED6.green_cathode
  N14: R3.Pin_1, LED6.blue_cathode
