# Fritzing sketch 632-PIANO (saved by Fritzing 0.9.0b)
breadboards: 1

parts:
  Part1 = Arduino Uno (Rev3)
  J1 = Piezo Speaker
  S1 = Momentary Switch [package=ksa_sealed_tac_switch]
  S2 = Momentary Switch [package=ksa_sealed_tac_switch]
  S3 = Momentary Switch [package=ksa_sealed_tac_switch]
  S4 = Momentary Switch [package=ksa_sealed_tac_switch]
  S5 = Momentary Switch [package=ksa_sealed_tac_switch]
  S6 = Momentary Switch [package=ksa_sealed_tac_switch]
  S7 = Momentary Switch [package=ksa_sealed_tac_switch]
  S8 = Momentary Switch [package=ksa_sealed_tac_switch]

nets:
  N1: Part1.D8, S6.1
  N2: Part1.D9_PWM, S5.1
  N3: Part1.D10_PWM/SS, S4.1
  N4: Part1.D11_PWM/MOSI, S3.1
  N5: Part1.D12/MISO, S2.1
  N6: Part1.D13/SCK, S1.1
  N7: Part1.GND, J1.pin1, S1.4, S2.4, S3.4, S4.4, S5.4, S6.4, S7.4, S8.4
  N8: Part1.D3_PWM, J1.pin2
  N9: Part1.D6_PWM, S8.1
  N10: Part1.D7, S7.1
