# Fritzing sketch 72-STANJETIPKALASERIAL (saved by Fritzing 0.9.0b)
breadboards: 1

parts:
  Part1 = Arduino Uno (Rev3)
  S1 = Momentary Switch [package=ksa_sealed_tac_switch]

nets:
  N1: Part1.D3_PWM, S1.1
  N2: Part1.GND, S1.4
