# Fritzing sketch 812-POTENCIOMETAR_ALED (saved by Fritzing 0.9.0b)
breadboards: 1

parts:
  Part1 = Arduino Uno (Rev3)
  R1 = Resistor [tolerance=±5% resistance=330 package=THT]
  LED1 = LED - 5mm [color="Red (635nm)" package="5 mm [THT]"]
  R2 = Trimmer Potentiometer [maximum_resistance=10kΩ package=THT]

nets:
  N1: Part1.A0, R2.wiper
  N2: Part1.GND, LED1.cathode, R2.leg2
  N3: Part1.D3_PWM, R1.Pin_0
  N4: Part1.5V, R2.leg1
  N5: R1.Pin_1, LED1.anode
