# Fritzing sketch 813-POTENCIOMETAR_RGB (saved by Fritzing 0.9.0b)
breadboards: 1

parts:
  Part1 = Arduino Uno (Rev3)
  R1 = Resistor [tolerance=±5% resistance=330 package=THT]
  R5 = Trimmer Potentiometer [maximum_resistance=10kΩ package=THT]
  R6 = Trimmer Potentiometer [maximum_resistance=10kΩ package=THT]
  R7 = Trimmer Potentiometer [maximum_resistance=10kΩ package=THT]
  LED1 = RGB LED - (4 legs) [package="5 mm [THT]"]
  R8 = Resistor [tolerance=±5% resistance=330 package=THT]
  R9 = Resistor [tolerance=±5% resistance=330 package=THT]

nets:
  N1: Part1.A0, R7.wiper
  N2: Part1.A1, R6.wiper
  N3: Part1.A2, R5.wiper
  N4: Part1.D3_PWM, R1.Pin_0
  N5: Part1.D5_PWM, R8.Pin_0
  N6: Part1.D6_PWM, R9.Pin_0
  N7: Part1.5V, R5.leg1, R6.leg1, R7.leg1, LED1.common_anode
  N8: Part1.GND, R5.leg2, R6.leg2, R7.leg2
  N9: R1.Pin_1, LED1.red_cathode
  N10: LED1.green_cathode, R8.Pin_1
  N11: LED1.blue_cathode, R9.Pin_1
