# Fritzing sketch 814-POTENCIOMETAR_DELAY (saved by Fritzing 0.9.0b)
breadboards: 1

parts:
  Part1 = Arduino Uno (Rev3)
  R5 = Trimmer Potentiometer [maximum_resistance=10kΩ package=THT]
  LED2 = LED - 5mm [color="Red (635nm)" package="5 mm [THT]"]
  LED3 = LED - 5mm [color="Red (635nm)" package="5 mm [THT]"]
  LED4 = LED - 5mm [color="Red (635nm)" package="5 mm [THT]"]
  LED5 = LED - 5mm [color="Red (635nm)" package="5 mm [THT]"]
  LED6 = LED - 5mm [color="Red (635nm)" package="5 mm [THT]"]
  R6 = Resistor [tolerance=±5% resistance=330 package=THT]
  R7 = Resistor [tolerance=±5% resistance=330 package=THT]
  R8 = Resistor [tolerance=±5% resistance=330 package=THT]
  R9 = Resistor [tolerance=±5% resistance=330 package=THT]
  R10 = Resistor [tolerance=±5% resistance=330 package=THT]

nets:
  N1: Part1.A0, R5.wiper
  N2: Part1.GND, R5.leg2, LED2.cathode, LED3.cathode, LED4.cathode, LED5.cathode, LED6.cathode
  N3: Part1.D2, R6.Pin_0
  N4: Part1.D3_PWM, R7.Pin_0
  N5: Part1.D4, R8.Pin_0
  N6: Part1.D5_PWM, R9.Pin_0
  N7: Part1.D6_PWM, R10.Pin_0
  N8: Part1.5V, R5.leg1
  N9: LED2.anode, R6.Pin_1
  N10: LED3.anode, R7.Pin_1
  N11: LED4.anode, R8.Pin_1
  N12: LED5.anode, R9.Pin_1
  N13: LED6.anode, R10.Pin_1
