# Fritzing sketch 822-FO_LED (saved by Fritzing 0.9.0b)
breadboards: 1

parts:
  Part1 = Arduino Uno (Rev3)
  R1 = Resistor [tolerance=±5% resistance=330 package=THT]
  LED1 = LED - 5mm [color="Red (635nm)" package="5 mm [THT]"]
  R2 = Resistor [tolerance=±5% resistance=10k package=THT]
  R7 = Photocell (LDR) [package=THT]

nets:
  N1: Part1.A0, R2.Pin_1, R7.pin_0
  N2: Part1.GND, LED1.cathode, R2.Pin_0
  N3: Part1.D3_PWM, R1.Pin_0
  N4: Part1.5V, R7.pin_1
  N5: R1.Pin_1, LED1.anode
